// Digital circuit alu.dig as structural Verilog
module alu (
  input  [31:0] A,
  input  [31:0] B,
  input  Sub,
  input  [1:0] Bool,
  input  [1:0] Op,
  output FlagZ,
  output [31:0] Out
);

  wire add_sub_1_overflow, add_sub_1_sign;
  wire [0:0] comparator_1_result;
  wire [31:0] add_sub_1_out, boolean_unit_1_out, shifter_1_out;

  add_sub add_sub_1 (
    .B(B), .A(A), .Sub(Sub), .Out(add_sub_1_out), .Overflow(add_sub_1_overflow), .Sign(add_sub_1_sign));
  comparator comparator_1 (.Sign(add_sub_1_sign), .Overflow(add_sub_1_overflow), .Result(comparator_1_result[0]));
  shifter shifter_1 (.A(A), .B(B), .Bool(Bool), .Out(shifter_1_out));
  Multiplexer #(.Selector_Bits(2), .Bits(32)) multiplexer_1 (
    .sel(Op), .in_0(add_sub_1_out), .in_1({{31{1'b0}}, comparator_1_result[0]}), .in_2(shifter_1_out),
    .in_3(boolean_unit_1_out), .out(Out));
  boolean_unit boolean_unit_1 (.A(A), .B(B), .Bool(Bool), .Out(boolean_unit_1_out));
  nor nor_1 (FlagZ, Out[0], Out[1], Out[2], Out[3], Out[4], Out[5], Out[6], Out[7], Out[8], Out[9], Out[10], Out[11], Out[12], Out[13], Out[14], Out[15], Out[17], Out[18], Out[19], Out[20], Out[21], Out[22], Out[23], Out[24], Out[25], Out[26], Out[27], Out[28], Out[29], Out[30], Out[31], Out[16]);

  // Notes on the sheet:
  //   Control Bits
  //   Inputs
  //   Outputs
endmodule

/* Test case ALU Test:
A B Sub Bool Op FlagZ Out

# Add - Sub 
0x289322C4 0x01846399 0 x 0b00 0 0x2A17865D 
0x4152A22D 0x22042121 0 x 0b00 0 0x6356C34E 
0x84893212 0x0994AD1A 0 x 0b00 0 0x8E1DDF2C 
0x90A8826C 0x112109FB 0 x 0b00 0 0xA1C98C67 
0x5210C12D 0x3D04ABBC 0 x 0b00 0 0x8F156CE9 
0x90D194B5 0xB005500E 0 x 0b00 0 0x40D6E4C3 
0x39332544 0x0435FCAD 1 x 0b00 0 0x34FD2897 
0x59286AB1 0x221FB76C 1 x 0b00 0 0x3708B345
0xECD55935 0x248C5A4B 1 x 0b00 0 0xC848FEEA 
0x902A9525 0xE5454D48 1 x 0b00 0 0xAAE547DD 
0x8211036A 0x7B13890A 1 x 0b00 0 0x06FD7A60
0x5FE15DBE 0x8934B9B1 1 x 0b00 0 0xD6ACA40D 

# Bidirectional Shifter
0x43927735 0x310e576d x 0 0b10 1 0x00000000
0x20693682 0x85050a62 x 0 0b10 0 0x14142988
0x737a6607 0x00b80c2b x 0 0b10 0 0x5c061580
0x3629b085 0xe3088aeb x 1 0b10 1 0x00000000
0x8403f72b 0xdc5ece59 x 1 0b10 1 0x00000000
0xae0824c7 0xbe187159 x 1 0b10 1 0x00000000
0xcb126889 0x0614e24a x 2 0b10 0 0x00030a71
0x02352d86 0x54891132 x 2 0b10 0 0x01522444
0x00000001 0xF0000000 x 2 0b10 0 0x78000000
0xf77f1486 0x18e2f036 x 2 0b10 0 0x00638bc0
0x289a9211 0x6d349ef7 x 3 0b10 0 0x0000369a
0x3b9a2707 0xe9349ed3 x 3 0b10 0 0xffd2693d
0x22853218 0xd175490b x 3 0b10 0 0xffffffd1


# Boolean Unit Tests
0xdcd84709 0x768a5af3 x 0 0b11 0 0x54884201
0x3d2cd361 0xf53106ef x 0 0b11 0 0x35200261
0x28f56e63 0x854b7d0b x 0 0b11 0 0x00416c03
0x9201A3De 0x2D1A9F88 x 1 0b11 0 0xBF1BBFDe
0xd15a7517 0xb900f275 x 1 0b11 0 0xf95af777
0xd81daa93 0x0ab5e9f7 x 1 0b11 0 0xdabdebf7
0x0f9eda3f 0x885e0a47 x 2 0b11 0 0x87c0d078
0xca58eed8 0x514af1fa x 2 0b11 0 0x9b121f22
0xc7100004 0x3553ef1e x 2 0b11 0 0xf243ef1a
0xd9537eed 0x133929ec x 3 0b11 0 0x24848012
0x66b776e8 0xb2aa434b x 3 0b11 0 0x09408814
0x745d1dab 0xafc46d88 x 3 0b11 0 0x00228254

# Comparator
0x289322C4 0x01846399 0 x 0b01 1 0x0
0x4152A22D 0x22042121 0 x 0b01 1 0x0 
0x84893212 0x0994AD1A 0 x 0b01 0 0x1 
0x90A8826C 0x112109FB 0 x 0b01 0 0x1 
0x5210C12D 0x3D04ABBC 0 x 0b01 1 0x0 
0x90D194B5 0xB005500E 0 x 0b01 0 0x1 
0x39332544 0x0435FCAD 1 x 0b01 1 0x0 
0x59286AB1 0x221FB76C 1 x 0b01 1 0x0
0xECD55935 0x248C5A4B 1 x 0b01 0 0x1 
0x902A9525 0xE5454D48 1 x 0b01 0 0x1 
0x8211036A 0x7B13890A 1 x 0b01 0 0x1
0x5FE15DBE 0x8934B9B1 1 x 0b1 1 0x0
*/
