// Digital circuit register-file.dig as structural Verilog
module register_file (
  input  [4:0] ReadReg1,
  input  [4:0] ReadReg2,
  input  [4:0] WriteReg,
  input  [31:0] WriteData,
  input  RegWrite,
  input  Clock,
  output [31:0] ReadData1,
  output [31:0] ReadData2
);

  wire dec0, dec1, dec2, dec3, dec4, dec5, dec6, dec7, dec8, dec9, dec10, dec11, dec12, dec13, dec14, dec15,
       dec16, dec17, dec18, dec19, dec20, dec21, dec22, dec23, dec24, dec25, dec26, dec27, dec28, dec29,
       dec30, dec31, w0, w1, w2, w3, w4, w5, w6, w7, w8, w9, w10, w11, w12, w13, w14, w15, w16, w17, w18,
       w19, w20, w21, w22, w23, w24, w25, w26, w27, w28, w29, w30, w31;
  wire [31:0] rx0_out, rx1_out, rx2_out, rx3_out, rx4_out, rx5_out, rx6_out, rx7_out, rx8_out, rx9_out,
       rx10_out, rx11_out, rx12_out, rx13_out, rx14_out, rx15_out, rx16_out, rx17_out, rx18_out, rx19_out,
       rx20_out, rx21_out, rx22_out, rx23_out, rx24_out, rx25_out, rx26_out, rx27_out, rx28_out, rx29_out,
       rx30_out, rx31_out;

  Register #(.Bits(32)) rx0 (.D({32{1'b0}}), .C(Clock), .en(1'b0), .Q(rx0_out));
  Register #(.Bits(32)) rx6 (.D(WriteData), .C(Clock), .en(w6), .Q(rx6_out));
  Register #(.Bits(32)) rx12 (.D(WriteData), .C(Clock), .en(w12), .Q(rx12_out));
  Register #(.Bits(32)) rx18 (.D(WriteData), .C(Clock), .en(w18), .Q(rx18_out));
  Register #(.Bits(32)) rx24 (.D(WriteData), .C(Clock), .en(w24), .Q(rx24_out));
  Register #(.Bits(32)) rx1 (.D(WriteData), .C(Clock), .en(w1), .Q(rx1_out));
  Register #(.Bits(32)) rx7 (.D(WriteData), .C(Clock), .en(w7), .Q(rx7_out));
  Register #(.Bits(32)) rx13 (.D(WriteData), .C(Clock), .en(w13), .Q(rx13_out));
  Register #(.Bits(32)) rx19 (.D(WriteData), .C(Clock), .en(w19), .Q(rx19_out));
  Register #(.Bits(32)) rx25 (.D(WriteData), .C(Clock), .en(w25), .Q(rx25_out));
  Register #(.Bits(32)) rx30 (.D(WriteData), .C(Clock), .en(w30), .Q(rx30_out));
  Register #(.Bits(32)) rx2 (.D(WriteData), .C(Clock), .en(w2), .Q(rx2_out));
  Register #(.Bits(32)) rx8 (.D(WriteData), .C(Clock), .en(w8), .Q(rx8_out));
  Register #(.Bits(32)) rx14 (.D(WriteData), .C(Clock), .en(w14), .Q(rx14_out));
  Register #(.Bits(32)) rx20 (.D(WriteData), .C(Clock), .en(w20), .Q(rx20_out));
  Register #(.Bits(32)) rx26 (.D(WriteData), .C(Clock), .en(w26), .Q(rx26_out));
  Register #(.Bits(32)) rx3 (.D(WriteData), .C(Clock), .en(w3), .Q(rx3_out));
  Register #(.Bits(32)) rx9 (.D(WriteData), .C(Clock), .en(w9), .Q(rx9_out));
  Register #(.Bits(32)) rx15 (.D(WriteData), .C(Clock), .en(w15), .Q(rx15_out));
  Register #(.Bits(32)) rx21 (.D(WriteData), .C(Clock), .en(w21), .Q(rx21_out));
  Register #(.Bits(32)) rx27 (.D(WriteData), .C(Clock), .en(w27), .Q(rx27_out));
  Register #(.Bits(32)) rx31 (.D(WriteData), .C(Clock), .en(w31), .Q(rx31_out));
  Register #(.Bits(32)) rx4 (.D(WriteData), .C(Clock), .en(w4), .Q(rx4_out));
  Register #(.Bits(32)) rx10 (.D(WriteData), .C(Clock), .en(w10), .Q(rx10_out));
  Register #(.Bits(32)) rx16 (.D(WriteData), .C(Clock), .en(w16), .Q(rx16_out));
  Register #(.Bits(32)) rx22 (.D(WriteData), .C(Clock), .en(w22), .Q(rx22_out));
  Register #(.Bits(32)) rx28 (.D(WriteData), .C(Clock), .en(w28), .Q(rx28_out));
  Register #(.Bits(32)) rx5 (.D(WriteData), .C(Clock), .en(w5), .Q(rx5_out));
  Register #(.Bits(32)) rx11 (.D(WriteData), .C(Clock), .en(w11), .Q(rx11_out));
  Register #(.Bits(32)) rx17 (.D(WriteData), .C(Clock), .en(w17), .Q(rx17_out));
  Register #(.Bits(32)) rx23 (.D(WriteData), .C(Clock), .en(w23), .Q(rx23_out));
  Register #(.Bits(32)) rx29 (.D(WriteData), .C(Clock), .en(w29), .Q(rx29_out));
  and and_1 (w0, RegWrite, dec0);
  and and_2 (w1, RegWrite, dec1);
  and and_3 (w2, RegWrite, dec2);
  and and_4 (w3, RegWrite, dec3);
  and and_5 (w4, RegWrite, dec4);
  and and_6 (w5, RegWrite, dec5);
  and and_7 (w6, RegWrite, dec6);
  and and_8 (w7, RegWrite, dec7);
  and and_9 (w8, RegWrite, dec8);
  and and_10 (w9, RegWrite, dec9);
  and and_11 (w10, RegWrite, dec10);
  and and_12 (w11, RegWrite, dec11);
  and and_13 (w12, RegWrite, dec12);
  and and_14 (w13, RegWrite, dec13);
  and and_15 (w14, RegWrite, dec14);
  and and_16 (w15, RegWrite, dec15);
  and and_17 (w16, RegWrite, dec16);
  and and_18 (w17, RegWrite, dec17);
  and and_19 (w18, RegWrite, dec18);
  and and_20 (w19, RegWrite, dec19);
  and and_21 (w20, RegWrite, dec20);
  and and_22 (w21, RegWrite, dec21);
  and and_23 (w22, RegWrite, dec22);
  and and_24 (w23, RegWrite, dec23);
  and and_25 (w24, RegWrite, dec24);
  and and_26 (w25, RegWrite, dec25);
  and and_27 (w26, RegWrite, dec26);
  and and_28 (w27, RegWrite, dec27);
  and and_29 (w28, RegWrite, dec28);
  and and_30 (w29, RegWrite, dec29);
  and and_31 (w30, RegWrite, dec30);
  and and_32 (w31, RegWrite, dec31);
  Multiplexer #(.Selector_Bits(5), .Bits(32)) multiplexer_1 (
    .sel(ReadReg2), .in_0(rx0_out), .in_1(rx1_out), .in_2(rx2_out), .in_3(rx3_out), .in_4(rx4_out),
    .in_5(rx5_out), .in_6(rx6_out), .in_7(rx7_out), .in_8(rx8_out), .in_9(rx9_out), .in_10(rx10_out),
    .in_11(rx11_out), .in_12(rx12_out), .in_13(rx13_out), .in_14(rx14_out), .in_15(rx15_out),
    .in_16(rx16_out), .in_17(rx17_out), .in_18(rx18_out), .in_19(rx19_out), .in_20(rx20_out),
    .in_21(rx21_out), .in_22(rx22_out), .in_23(rx23_out), .in_24(rx24_out), .in_25(rx25_out),
    .in_26(rx26_out), .in_27(rx27_out), .in_28(rx28_out), .in_29(rx29_out), .in_30(rx30_out),
    .in_31(rx31_out), .out(ReadData2));
  Decoder #(.Selector_Bits(5)) decoder_1 (
    .sel(WriteReg), .out_0(dec0), .out_1(dec1), .out_2(dec2), .out_3(dec3), .out_4(dec4), .out_5(dec5),
    .out_6(dec6), .out_7(dec7), .out_8(dec8), .out_9(dec9), .out_10(dec10), .out_11(dec11), .out_12(dec12),
    .out_13(dec13), .out_14(dec14), .out_15(dec15), .out_16(dec16), .out_17(dec17), .out_18(dec18),
    .out_19(dec19), .out_20(dec20), .out_21(dec21), .out_22(dec22), .out_23(dec23), .out_24(dec24),
    .out_25(dec25), .out_26(dec26), .out_27(dec27), .out_28(dec28), .out_29(dec29), .out_30(dec30),
    .out_31(dec31));
  Multiplexer #(.Selector_Bits(5), .Bits(32)) multiplexer_2 (
    .sel(ReadReg1), .in_0(rx0_out), .in_1(rx1_out), .in_2(rx2_out), .in_3(rx3_out), .in_4(rx4_out),
    .in_5(rx5_out), .in_6(rx6_out), .in_7(rx7_out), .in_8(rx8_out), .in_9(rx9_out), .in_10(rx10_out),
    .in_11(rx11_out), .in_12(rx12_out), .in_13(rx13_out), .in_14(rx14_out), .in_15(rx15_out),
    .in_16(rx16_out), .in_17(rx17_out), .in_18(rx18_out), .in_19(rx19_out), .in_20(rx20_out),
    .in_21(rx21_out), .in_22(rx22_out), .in_23(rx23_out), .in_24(rx24_out), .in_25(rx25_out),
    .in_26(rx26_out), .in_27(rx27_out), .in_28(rx28_out), .in_29(rx29_out), .in_30(rx30_out),
    .in_31(rx31_out), .out(ReadData1));

  // Other names for the same wires on the sheet: CLK = Clock; RD1[31:0] = ReadData1; RD2[31:0] = ReadData2;
  //   RR1[4:0] = ReadReg1; RR2[4:0] = ReadReg2; RW = RegWrite; WD[31:0] = WriteData; WR[4:0] = WriteReg
endmodule

/* Test case Register File Test:
WriteReg WriteData RegWrite Clock ReadReg1 ReadReg2 ReadData1 ReadData2

# $1 = 25
1 25 1 C 1 0 25 0

# $2 = 30
2 30 1 C 0 2 0 30

# $(N+1) = (N+1)
loop(N, 30)
	(N+1) (N+1) 1 C (N+1) (N) (N+1) (N)
end loop

# $(N+1) = N-60
loop(N, 30)
	(N+1) (N-60) 1 C (N+1) (N+1) (N-60) (N-60)
end loop

# Try writing to $0. This should not write anything
0 25 1 C 0 0 0 0

# try writing when RegWrite = 0
# (the registers should still have their old values)
loop(N, 30)
	(N+1) (N+80) 0 C (N+1) (N+1) (N-60) (N-60)
end loop
*/
